# Fritzing sketch ControlPerfBoardMotor (saved by Fritzing 0.9.1b)
perfboards: 1

parts:
  Parte1 = Arduino Leonardo (Rev3b)
  VCC1 = Battery [part_number="Ultrafire 7,4V 6000mAH"]
  M1 = DC Motor
  M2 = DC Motor
  IC1 = L293D [package=THT]

nets:
  N1: Parte1.D2/SDA, Parte1.SDA, IC1.In_1
  N2: Parte1.D3_PWM/SCL, Parte1.SCL, IC1.+Vmotor
  N3: Parte1.D4/A6, IC1.In_3
  N4: Parte1.D5_PWM, IC1.In_4
  N5: Parte1.GND, VCC1.-, IC1.0V
  N6: Parte1.VIN, VCC1.+, IC1.+V
  N7: Parte1.D8/A8, IC1.Enable_1
  N8: Parte1.D9_PWM/A9, IC1.Enable_2
  N9: M1.pin_1, IC1.Out_3_(_Controlled_by_Enable_2_)
  N10: M1.pin_2, IC1.Out_4_(_Controlled_by_Enable_2_)
  N11: M2.pin_1, IC1.Out_1_(_Controlled_by_Enable_1_)
  N12: M2.pin_2, IC1.In_2

notes:
  Azul: B
  Amarillo: F
  Blanco: L
  Verde: R

// code stored in the sketch: Control.ino
int ledPin = 2;                 // LED connected to digital pin 13

void setup()
{
  pinMode(ledPin, OUTPUT);      // sets the digital pin as output
}

void loop()
{
  digitalWrite(ledPin, HIGH);   // sets the LED on
  delay(2000);                  // waits for a second
  digitalWrite(ledPin, LOW);    // sets the LED off
  delay(2000);                  // waits for a second
}
